// Logisim project SAP1_matheus Release.circ as structural Verilog: 11 circuits, main circuit main
module main (
  input  Reset,
  output [3:0] Dados,
  output [3:0] \Dados___Endereços ,
  output out_4,
  output out_5,
  output out_6,
  output out_7,
  output out_8,
  output out_9,
  output out_10,
  output out_11
);

  wire CLK, Clock_out, controlador_sequencializador_rom_1_hlt, Cp, Dec, Div, Ea, Ep, Eu, Inc, Lp, Mul, nCE,
       nEi, nLa, nLb, nLi, nLm, nLo, Not, not_1_out, not_2_out, not_3_out, not_4_out,
       \registrador_instruções_1_i4 , \registrador_instruções_1_i5 , \registrador_instruções_1_i6 ,
       \registrador_instruções_1_i7 , Sav, Sqr, Su;
  wire [3:0] rem_1_remout;
  wire [7:0] acumulador_1_a_out_ula, counter_1_q, registrador_b_1_b_dataout;

  Clock Clock (.out(Clock_out));
  assign CLK = not_1_out ? Clock_out : 1'bz;  // Controlled_Buffer controlled_buffer_1
  not not_1 (not_1_out, controlador_sequencializador_rom_1_hlt);
  not not_2 (not_2_out, CLK);
  not not_3 (not_3_out, Reset);
  not not_4 (not_4_out, nCE);
  Contador_Programa contador_programa_1 (
    .Cp(Cp), .nCLK(not_2_out), .nCLR(not_3_out), .Ep(Ep), .Cp_Out(\Dados___Endereços ), .Lp(Lp),
    .Cp_In(\Dados___Endereços ));
  REM rem_1 (.in_1(\Dados___Endereços ), .nLm(nLm), .CLK(CLK), .REMOut(rem_1_remout));
  \Memória_RAM  \memória_ram_1  (
    .in_1(rem_1_remout), .nCE(not_4_out), .CLK(CLK), .out_6({Dados, \Dados___Endereços }), .Sav(Sav),
    .in_2({Dados, \Dados___Endereços }));
  \Registrador_Instruções  \registrador_instruções_1  (
    .in_1({Dados, \Dados___Endereços }), .nLi(nLi), .CLK(CLK), .CLR(Reset), .nEi(nEi),
    .out_6(\Dados___Endereços ), .I4(\registrador_instruções_1_i4 ), .I5(\registrador_instruções_1_i5 ),
    .I6(\registrador_instruções_1_i6 ), .I7(\registrador_instruções_1_i7 ));
  Controlador_Sequencializador_ROM controlador_sequencializador_rom_1 (
    .CLK(CLK), .CLR(Reset), .HLT(controlador_sequencializador_rom_1_hlt), .Cp(Cp), .Ep(Ep), .nLm(nLm),
    .nCE(nCE), .nLl(nLi), .nEl(nEi), .nLa(nLa), .Ea(Ea), .Su(Su), .Eu(Eu), .nLb(nLb), .nLo(nLo),
    .I7(\registrador_instruções_1_i7 ), .I6(\registrador_instruções_1_i6 ),
    .I4(\registrador_instruções_1_i4 ), .Inc(Inc), .Dec(Dec), .Mul(Mul), .Lp(Lp),
    .I5(\registrador_instruções_1_i5 ), .Sqr(Sqr), .Div(Div), .Not(Not), .Sav(Sav));
  Acumulador acumulador_1 (
    .A_In({Dados, \Dados___Endereços }), .nLa(nLa), .CLK(CLK), .Ea(Ea), .A_Out_ULA(acumulador_1_a_out_ula),
    .A_Out({Dados, \Dados___Endereços }));
  ULA ula_1 (
    .Su(Su), .B_data(registrador_b_1_b_dataout), .A_dataOut2({Dados, \Dados___Endereços }),
    .A_data(acumulador_1_a_out_ula), .Eu(Eu), .inc(Inc), .dec(Dec), .Mul(Mul), .Div(Div), .Sqr(Sqr), .Not(Not));
  Registrador_B registrador_b_1 (
    .B_dataIn({Dados, \Dados___Endereços }), .B_dataOut(registrador_b_1_b_dataout), .nLb(nLb), .CLK(CLK));
  Hex_Digit_Display hex_digit_display_1 (.value({out_4, out_5, out_6, out_7}));  // open: dp
  \Indicação_Visual  \indicação_visual_1  (
    .Input({Dados, \Dados___Endereços }),
    .Output({out_4, out_5, out_6, out_7, out_8, out_9, out_10, out_11}), .nLo(nLo), .CLK(CLK), .CLR(Reset));
  DotMatrix #(.matrixcols(8), .matrixrows(1), .dotshape("circle")) dotmatrix_1 (
    .col0(out_4), .col1(out_5), .col2(out_6), .col3(out_7), .col4(out_8), .col5(out_9), .col6(out_10),
    .col7(out_11));
  Hex_Digit_Display hex_digit_display_2 (.value({out_8, out_9, out_10, out_11}));  // open: dp
  Counter counter_1 (.Q(counter_1_q), .clk(CLK), .clr(Reset));  // open: load, D, count, carry
  Hex_Digit_Display hex_digit_display_3 (.value(counter_1_q[3:0]));  // open: dp
  Hex_Digit_Display hex_digit_display_4 (.value(counter_1_q[7:4]));  // open: dp

  // Other names for the same wires on the sheet: CLR = Reset

  // Notes on the sheet:
  //   SAP-1 em LOGISIM Modificado Matheus Ver1.0 /2024
  //   Arquitetura de Computadores I
  //   BIT 4
  //   BIT 3
  //   I
  //   I
  //   BIT 2
  //   I
  //   BIT1
  //   Grupo (individual)**:
  //   - Matheus Silva Coxir
  //   Instruções Padrão:
  //   Load Accumulator    LDA 0000: A<-*(MEM)
  //   Add   ADD 0001: A<= A+B
  //   Subtract   SUB 0010: A<= A-B
  //   Output   OUT 1110: Exibir o valor
  //   Halt   HLT 1111: Interromper o circuito
  //   Instruções Novas:
  //   Increment   INC 0011: A<= A+1
  //   Decrement   DEC 0100: A<= A-1
  //   Multiply   MUL 0101: A<= AxB
  //   Jump   JMP 0110: CP<- endereço de salto
  //   NOT   NOT 1001: A <= -A
  //   Divide   Div 1000: A <= A/B
  //   Square   Sqr 0111: A <= A²
  //   Save   Sav 1010: *(MEM) <= A
  //   Como usar:
  //   Adicione as operações no bloco de memória RAM,
  //   execute um RESET e envie pulsos de clock.
  //   ** Esse trabalho foi uma modificação do trabalho feito por:
  //   - André Luís Silva de Paula
  //   - André Santos Alves
  //   - Nathan de Araújo Cunha Lisboa
  //   - Pedro Malta Boscatti
  //   - Sophia Damasceno Satuf
  //   As modificações foram feitas no controlador sequencializador e na ULA.
endmodule

module Contador_Programa (
  input  Lp,
  input  [3:0] Cp_In,
  input  Cp,
  input  nCLK,
  input  nCLR,
  input  Ep,
  output [3:0] Cp_Out
);

  wire not_1_out;
  wire [3:0] counter_1_q;

  not not_1 (not_1_out, nCLR);
  Counter #(.width(4), .max('hf), .trigger("falling")) counter_1 (
    .load(Lp), .D(Cp_In), .count(Cp), .Q(counter_1_q), .clk(nCLK), .clr(not_1_out));  // open: carry
  assign Cp_Out = Ep ? counter_1_q : 4'bz;  // Controlled_Buffer controlled_buffer_1
endmodule

module REM (
  input  [3:0] in_1,
  input  nLm,
  input  CLK,
  output [3:0] REMOut
);

  wire not_1_out;

  not not_1 (not_1_out, nLm);
  Register #(.width(4)) register_1 (.D(in_1), .en(not_1_out), .Q(REMOut), .clk(CLK));  // open: clr
endmodule

module \Memória_RAM  (
  input  [3:0] in_1,
  input  [7:0] in_2,
  input  nCE,
  input  CLK,
  input  Sav,
  output [7:0] out_6
);

  wire and_1_out, not_1_out, or_1_out;
  wire [7:0] ram_1_data;

  or or_1 (or_1_out, nCE, Sav);
  and and_1 (and_1_out, nCE, not_1_out);
  not not_1 (not_1_out, Sav);
  RAM #(.addrWidth(4)) ram_1 (.addr(in_1), .data(ram_1_data), .sel(or_1_out), .clk(CLK), .ld(and_1_out));  // open: clr
  assign out_6 = nCE ? ram_1_data : 8'bz;  // Controlled_Buffer controlled_buffer_1
  assign ram_1_data = Sav ? in_2 : 8'bz;  // Controlled_Buffer controlled_buffer_2

  // Notes on the sheet:
  //   Operações:
  //   Exemplo 1:  02 + 03 - 04 + 02 = 03
  //   0f e0 1e e0 2d e0 1f e0 f0 00 00 00 00 04 03 02
  //   Exemplo 2:  150 + 70 - 50 + 100 = ? 270
  //   0f e0 1e e0 2d e0 1c e0 f0 00 00 00 64 32 46 96
  //   Exemplo 3:  5 x 2 - 1 - 2 + 1 = 8
  //   0f e0 5e e0 40 e0 2e e0 30 e0 f0 00 00 00 02 05
  //   Exemplo 4:  Carrega A=1,Exibe A, Inc A, Exibe A, JMP para Inc A 
  //   0f e0 30 e0 62 f0
  //   Exemplo 5: (Fibonacci) 1-> 2 -> 3 -> 5 -> 8 -> 13 -> 21..
  //   Exemplo 6: (Função) func(4) + 1 -> Exibe -> -3 -> Exibe
  //   func(4) -> (4²/2 )* 3) --> Exibe
endmodule

module \Registrador_Instruções  (
  input  [7:0] in_1,
  input  nLi,
  input  CLK,
  input  CLR,
  input  nEi,
  output [3:0] out_6,
  output I4,
  output I5,
  output I6,
  output I7
);

  wire not_1_out, not_2_out;
  wire [3:0] register_1_q;

  not not_1 (not_1_out, nLi);
  not not_2 (not_2_out, nEi);
  Register register_1 (.D(in_1), .en(not_1_out), .Q({I7, I6, I5, I4, register_1_q}), .clk(CLK), .clr(CLR));
  assign out_6 = not_2_out ? register_1_q : 4'bz;  // Controlled_Buffer controlled_buffer_1
endmodule

module Acumulador (
  input  [7:0] A_In,
  input  nLa,
  input  CLK,
  input  Ea,
  output [7:0] A_Out_ULA,
  output [7:0] A_Out
);

  wire not_1_out;

  not not_1 (not_1_out, nLa);
  Register register_1 (.D(A_In), .en(not_1_out), .Q(A_Out_ULA), .clk(CLK));  // open: clr
  assign A_Out = Ea ? A_Out_ULA : 8'bz;  // Controlled_Buffer controlled_buffer_1
endmodule

module ULA (
  input  Su,
  input  inc,
  input  dec,
  input  [7:0] B_data,
  input  [7:0] A_data,
  input  Eu,
  input  Sqr,
  input  Mul,
  input  Div,
  input  Not,
  output [7:0] A_dataOut2
);

  wire not_1_out, not_2_out, or_1_out, or_2_out;
  wire [7:0] adder_1_out, controlled_buffer_1_out, controlled_buffer_3_out, divider_1_out, multiplier_1_out,
       negator_1_out, xor_1_out;

  or or_1 (or_1_out, inc, dec);
  not not_1 (not_1_out, or_1_out);
  assign controlled_buffer_1_out = or_1_out ? 8'h1 : 8'bz;  // Controlled_Buffer controlled_buffer_1
  assign controlled_buffer_1_out = not_1_out ? B_data : 8'bz;  // Controlled_Buffer controlled_buffer_2
  assign controlled_buffer_3_out = not_2_out ? B_data : 8'bz;  // Controlled_Buffer controlled_buffer_3
  assign controlled_buffer_3_out = Sqr ? A_data : 8'bz;  // Controlled_Buffer controlled_buffer_4
  not not_2 (not_2_out, Sqr);
  or or_2 (or_2_out, Sqr, Mul);
  assign xor_1_out = {8{Su}} ^ controlled_buffer_1_out;  // XOR_Gate xor_1, 8 bits wide
  Adder adder_1 (.a(xor_1_out), .b(A_data), .out(adder_1_out), .cin(Su));  // open: cout
  Multiplier multiplier_1 (.a(controlled_buffer_3_out), .b(A_data), .out(multiplier_1_out));  // open: cin, cout
  Divider divider_1 (.a(A_data), .b(B_data), .out(divider_1_out));  // open: upper, rem
  Negator negator_1 (.in(A_data), .out(negator_1_out));
  assign A_dataOut2 = Eu ? adder_1_out : 8'bz;  // Controlled_Buffer controlled_buffer_5
  assign A_dataOut2 = or_2_out ? multiplier_1_out : 8'bz;  // Controlled_Buffer controlled_buffer_6
  assign A_dataOut2 = Div ? divider_1_out : 8'bz;  // Controlled_Buffer controlled_buffer_7
  assign A_dataOut2 = Not ? negator_1_out : 8'bz;  // Controlled_Buffer controlled_buffer_8
endmodule

module Registrador_B (
  input  [7:0] B_dataIn,
  input  nLb,
  input  CLK,
  output [7:0] B_dataOut
);

  wire not_1_out;

  Register register_1 (.D(B_dataIn), .en(not_1_out), .Q(B_dataOut), .clk(CLK));  // open: clr
  not not_1 (not_1_out, nLb);
endmodule

module Decodificador (
  input  l7,
  input  l6,
  input  l5,
  input  l4,
  output LDA,
  output ADD,
  output SUB,
  output OUT,
  output HLT
);

  wire and_1_out, and_2_out, and_3_out, and_4_out, and_5_out, not_1_out, not_2_out, not_3_out, not_4_out;

  not not_1 (not_1_out, l7);
  not not_2 (not_2_out, l6);
  not not_3 (not_3_out, l5);
  not not_4 (not_4_out, l4);
  and and_1 (and_1_out, not_1_out, not_2_out, not_3_out, not_4_out);
  buf buffer_1 (LDA, and_1_out);
  buf buffer_2 (ADD, and_2_out);
  and and_2 (and_2_out, not_1_out, not_2_out, not_3_out, l4);
  and and_3 (and_3_out, not_1_out, not_2_out, l5, not_4_out);
  buf buffer_3 (SUB, and_3_out);
  buf buffer_4 (OUT, and_4_out);
  and and_4 (and_4_out, l7, l6, l5, not_4_out);
  buf buffer_5 (HLT, and_5_out);
  and and_5 (and_5_out, l7, l6, l5, l4);
endmodule

module \Indicação_Visual  (
  input  [7:0] Input,
  input  nLo,
  input  CLK,
  input  CLR,
  output [7:0] Output
);

  wire not_1_out;

  not not_1 (not_1_out, nLo);
  Register register_1 (.D(Input), .en(not_1_out), .Q(Output), .clk(CLK), .clr(CLR));
endmodule

module Controlador_Sequencializador_ROM (
  input  I7,
  input  I6,
  input  I5,
  input  I4,
  input  CLK,
  input  CLR,
  output Cp,
  output Ep,
  output nLm,
  output nCE,
  output nLl,
  output nEl,
  output nLa,
  output Ea,
  output Su,
  output Eu,
  output nLb,
  output nLo,
  output Inc,
  output Dec,
  output Mul,
  output Lp,
  output Div,
  output Sqr,
  output Not,
  output Sav,
  output HLT
);

  wire and_2_out, and_3_out, and_5_out, clr_t, decoder_1_out9, decoder_1_out10, decoder_1_out11,
       decoder_1_out12, decoder_1_out13, decoder_1_out14, decoder_1_out15, load, nop, nor_1_out, not_1_out,
       not_2_out, not_3_out, or_1_out, or_3_out, shift_register_1_q0, shift_register_1_q1,
       shift_register_1_q3, shift_register_1_q4;
  wire [3:0] ram_1_data;
  wire [5:0] counter_1_q, rom_1_data;

  and and_1 (HLT, I7, I6, I5, I4);
  ROM #(.addrWidth(4), .dataWidth(6)) rom_1 (.addr({I7, I6, I5, I4}), .data(rom_1_data));  // open: sel
  or or_1 (or_1_out, CLR, nop);
  or or_2 (clr_t, or_1_out, nor_1_out);
  not not_1 (not_1_out, load);
  not not_2 (not_2_out, CLK);
  Shift_Register #(.length(6)) shift_register_1 (
    .in(nor_1_out), .clk(CLK), .clr(or_1_out), .q0(shift_register_1_q0), .q1(shift_register_1_q1), .q2(load),
    .q3(shift_register_1_q3), .q4(shift_register_1_q4));  // open: shift, out, load, d0, d1, d2, d3, d4, d5, q5
  Counter #(.width(6), .max('h3f), .ongoal("continue")) counter_1 (
    .load(load), .D(rom_1_data), .count(not_1_out), .Q(counter_1_q), .clk(not_2_out), .clr(clr_t));  // open: carry
  nor nor_1 (nor_1_out, shift_register_1_q0, shift_register_1_q1, load, shift_register_1_q3, shift_register_1_q4);
  RAM #(.addrWidth(6), .dataWidth(16)) ram_1 (
    .addr(counter_1_q), .data({Cp, Ep, nLm, nCE, nLl, nEl, nLa, Ea, Su, Eu, nLb, nLo, ram_1_data}));  // open: sel, clk, ld, clr
  and and_2 (and_2_out, ~Cp, ~Ep, nLm, nCE);  // AND_Gate
  and and_3 (and_3_out, nLl, nEl, nLa, ~Ea);  // AND_Gate
  and and_4 (nop, and_2_out, and_3_out, and_5_out, not_3_out);
  and and_5 (and_5_out, ~Su, ~Eu, nLb, nLo);  // AND_Gate
  or or_3 (or_3_out, ram_1_data[0], ram_1_data[1], ram_1_data[2], ram_1_data[3]);
  Decoder #(.select(4), .disabled(0), .enable("false")) decoder_1 (
    .out1(Inc), .out2(Dec), .out3(Mul), .out4(Lp), .out5(Div), .out6(Sqr), .out7(Not), .out8(Sav),
    .out9(decoder_1_out9), .out10(decoder_1_out10), .out11(decoder_1_out11), .out12(decoder_1_out12),
    .out13(decoder_1_out13), .out14(decoder_1_out14), .out15(decoder_1_out15), .sel(ram_1_data));  // open: out0
  not not_3 (not_3_out, or_3_out);

  // Notes on the sheet:
  //   contents of rom_1 (hex, n*v repeats v):
  //   3 6 9 10 12 14 17 19 1b 1e 20 0 0 0 c
endmodule
